# Fritzing sketch buscaminas (saved by Fritzing 0.9.2b)
breadboards: 1

parts:
  Part1 = Arduino Uno (Rev3)
  S1 = Pushbutton [package="[THT]"]
  S2 = Pushbutton [package="[THT]"]
  S3 = Pushbutton [package="[THT]"]
  J1 = Piezo Speaker
  Part2 = Thumb Joystick
  LED1 = LED - 5mm [color="Blue (430nm)" package="5 mm [THT]"]
  Nokia_5110_LCD_Module1 = Nokia5110LCDModule
  R1 = Resistor [tolerance=±5% resistance=10k package=THT]
  R2 = Resistor [tolerance=±5% resistance=10k package=THT]
  R3 = Resistor [tolerance=±5% resistance=10k package=THT]
  R4 = Resistor [tolerance=±5% resistance=10k package=THT]
  R5 = Resistor [tolerance=±5% resistance=1k package=THT]
  R6 = Resistor [tolerance=±5% resistance=330 package=THT]
  R7 = Resistor [tolerance=±5% resistance=10k package=THT]
  R8 = Resistor [tolerance=±5% resistance=10k package=THT]
  R9 = Resistor [tolerance=±5% resistance=10k package=THT]
  R10 = Resistor [tolerance=±5% resistance=47 package=THT]

nets:
  N1: Part1.A0, Part2.HORZ
  N2: Part1.A1, Part2.VERT
  N3: Part1.D8, J1.pin2
  N4: Part1.D12/MISO, S2.Pin_1, S2.Pin_2, R8.Pin_1
  N5: Part1.D13/SCK, S3.Pin_1, S3.Pin_2, R7.Pin_1
  N6: Part1.D2, S1.Pin_1, S1.Pin_2, R9.Pin_1
  N7: Part1.D3_PWM, R4.Pin_0
  N8: Part1.D4, R3.Pin_0
  N9: Part1.D5_PWM, R2.Pin_0
  N10: Part1.D6_PWM, R5.Pin_0
  N11: Part1.D7, R1.Pin_0
  3V3: Part1.3V3, Nokia_5110_LCD_Module1.Vcc
  5V: Part1.5V, S1.Pin_3, S1.Pin_4, S2.Pin_3, S2.Pin_4, S3.Pin_3, S3.Pin_4, Part2.VCC
  GND: Part1.GND, Part2.GND, Nokia_5110_LCD_Module1.Grnd, R6.Pin_0, R7.Pin_0, R8.Pin_0, R9.Pin_0, R10.Pin_0
  N12: J1.pin1, LED1.anode
  N13: LED1.cathode, R10.Pin_1
  N14: Nokia_5110_LCD_Module1.SCE, R5.Pin_1
  N15: Nokia_5110_LCD_Module1.RST, R1.Pin_1
  N16: Nokia_5110_LCD_Module1.D/C, R2.Pin_1
  N17: Nokia_5110_LCD_Module1.6_DN_(MOSI), R3.Pin_1
  N18: Nokia_5110_LCD_Module1.SCLK, R4.Pin_1
  N19: Nokia_5110_LCD_Module1.LED, R6.Pin_1

custom parts:
  : Nokia 5110 LCD with 8 pin. It's a 45mm*45mm module part. Description: The Nokia 5110 is a basic graphic LCD screen for lots of applications. It was originally intended for as a cell phone screen. This one is mounted on an easy to solder PCB. It uses the PCD8544 controller. The PCD8544 is a low power CMOS LCD controller/driver, designed to drive a graphic display of 48 rows and 84 columns. All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
